// Logisim project lab10.circ as structural Verilog: 4 circuits, main circuit main
module main (
  input  Clock
);

  wire Decoder_dstmux, Fields_register, not_1_out;
  wire [1:0] Decoder_alu;
  wire [3:0] Fields_opcode;
  wire [7:0] adder_1_out, ALU_p4, Fields_immediate, multiplexer_1_out, PC_q, Reg_A_q, Reg_B_q;
  wire [15:0] rom_1_data;

  Adder adder_1 (.a(PC_q), .b(8'h1), .out(adder_1_out));  // open: cin, cout
  Register PC (.D(adder_1_out), .en(1'b1), .Q(PC_q), .clk(Clock));  // open: clr
  ROM #(.dataWidth(16)) rom_1 (.addr(PC_q), .data(rom_1_data), .sel(1'b1));
  Fields Fields (
    .Instruction(rom_1_data), .Immediate(Fields_immediate), .Register(Fields_register), .Opcode(Fields_opcode));
  Decoder Decoder (.Opcode(Fields_opcode), .ALU(Decoder_alu), .DstMux(Decoder_dstmux));
  Multiplexer #(.width(8), .enable("false")) multiplexer_1 (
    .in0(ALU_p4), .in1(Fields_immediate), .out(multiplexer_1_out), .sel(Decoder_dstmux));
  not not_1 (not_1_out, Fields_register);
  Register Reg_A (.D(multiplexer_1_out), .en(not_1_out), .Q(Reg_A_q), .clk(Clock));  // open: clr
  Register Reg_B (.D(multiplexer_1_out), .en(Fields_register), .Q(Reg_B_q), .clk(Clock));  // open: clr
  // ALU ALU: pin names not known; wires that end beside it: Decoder_alu, Reg_A_q, Reg_B_q, ALU_p4
endmodule

module Fields (
  input  [15:0] Instruction,
  output [7:0] Immediate,
  output Register,
  output [3:0] Opcode
);


  assign Immediate = Instruction[7:0];
  assign Opcode = Instruction[15:12];
  assign Register = Instruction[11];
endmodule

module ALU (
  input  [7:0] A,
  input  [1:0] Operation,
  input  [7:0] B,
  output [7:0] Output
);

  wire [7:0] adder_1_out, and_1_out, or_1_out, subtractor_1_out;

  assign or_1_out = A | B;  // OR_Gate or_1, 8 bits wide
  assign and_1_out = A & B;  // AND_Gate and_1, 8 bits wide
  Adder adder_1 (.a(A), .b(B), .out(adder_1_out));  // open: cin, cout
  Subtractor subtractor_1 (.a(A), .b(B), .out(subtractor_1_out));  // open: bin, bout
  Multiplexer #(.select(2), .width(8), .enable("false")) multiplexer_1 (
    .in0(or_1_out), .in1(and_1_out), .in2(adder_1_out), .in3(subtractor_1_out), .out(Output), .sel(Operation));
endmodule

module Decoder (
  input  [3:0] Opcode,
  output [1:0] ALU,
  output DstMux
);

  wire or_1_out;

  not not_1 (DstMux, or_1_out);
  or or_1 (or_1_out, Opcode[0], Opcode[1], Opcode[2]);

  assign ALU = Opcode[1:0];
endmodule
