// Logisim project lab07.circ as structural Verilog: 2 circuits, main circuit main
module main (
  input  [7:0] Input
);

  wire bcd_to_seven_segment_1_a, bcd_to_seven_segment_1_b, bcd_to_seven_segment_1_c,
       bcd_to_seven_segment_1_d, bcd_to_seven_segment_1_e, bcd_to_seven_segment_1_f,
       bcd_to_seven_segment_1_g, bcd_to_seven_segment_1_h, bcd_to_seven_segment_2_a,
       bcd_to_seven_segment_2_b, bcd_to_seven_segment_2_c, bcd_to_seven_segment_2_d,
       bcd_to_seven_segment_2_e, bcd_to_seven_segment_2_f, bcd_to_seven_segment_2_g, bcd_to_seven_segment_2_h;

  BCD_to_Seven_Segment bcd_to_seven_segment_1 (
    .in_1(Input[7:4]), .A(bcd_to_seven_segment_1_a), .B(bcd_to_seven_segment_1_b),
    .C(bcd_to_seven_segment_1_c), .D(bcd_to_seven_segment_1_d), .E(bcd_to_seven_segment_1_e),
    .F(bcd_to_seven_segment_1_f), .G(bcd_to_seven_segment_1_g), .H(bcd_to_seven_segment_1_h));
  _7_Segment_Display u_7_segment_display_1 (
    .g(bcd_to_seven_segment_1_a), .f(bcd_to_seven_segment_1_b), .a(bcd_to_seven_segment_1_c),
    .b(bcd_to_seven_segment_1_d), .e(bcd_to_seven_segment_1_e), .d(bcd_to_seven_segment_1_f),
    .c(bcd_to_seven_segment_1_g), .dp(bcd_to_seven_segment_1_h));
  BCD_to_Seven_Segment bcd_to_seven_segment_2 (
    .in_1(Input[3:0]), .A(bcd_to_seven_segment_2_a), .B(bcd_to_seven_segment_2_b),
    .C(bcd_to_seven_segment_2_c), .D(bcd_to_seven_segment_2_d), .E(bcd_to_seven_segment_2_e),
    .F(bcd_to_seven_segment_2_f), .G(bcd_to_seven_segment_2_g), .H(bcd_to_seven_segment_2_h));
  _7_Segment_Display u_7_segment_display_2 (
    .g(bcd_to_seven_segment_2_a), .f(bcd_to_seven_segment_2_b), .a(bcd_to_seven_segment_2_c),
    .b(bcd_to_seven_segment_2_d), .e(bcd_to_seven_segment_2_e), .d(bcd_to_seven_segment_2_f),
    .c(bcd_to_seven_segment_2_g), .dp(bcd_to_seven_segment_2_h));
endmodule

module BCD_to_Seven_Segment (
  input  [3:0] in_1,
  output A,
  output B,
  output C,
  output D,
  output E,
  output F,
  output G,
  output H
);

  wire and_1_out, and_2_out, and_3_out, and_4_out, and_5_out, and_6_out, and_7_out, and_8_out, and_9_out,
       and_10_out, and_11_out, and_12_out, and_13_out, and_14_out, and_15_out, and_16_out, and_17_out,
       and_18_out, and_19_out, and_20_out, and_21_out, and_22_out, and_23_out, and_24_out, and_25_out,
       and_26_out, not_1_out, not_2_out, not_3_out, not_4_out;

  not not_1 (not_1_out, in_1[3]);
  not not_2 (not_2_out, in_1[2]);
  not not_3 (not_3_out, in_1[1]);
  not not_4 (not_4_out, in_1[0]);
  and and_1 (and_1_out, in_1[1], not_4_out);
  and and_2 (and_2_out, in_1[2], not_3_out);
  and and_3 (and_3_out, not_2_out, in_1[1]);
  and and_4 (and_4_out, not_4_out, not_3_out);
  and and_5 (and_5_out, in_1[2], not_4_out);
  and and_6 (and_6_out, in_1[2], not_3_out);
  and and_7 (and_7_out, not_2_out, not_4_out);
  and and_8 (and_8_out, in_1[2], in_1[0]);
  and and_9 (and_9_out, in_1[1], not_2_out);
  and and_10 (and_10_out, not_1_out, not_2_out);
  and and_11 (and_11_out, not_3_out, not_2_out);
  and and_12 (and_12_out, not_3_out, not_4_out, not_1_out);
  and and_13 (and_13_out, in_1[0], not_1_out, in_1[1]);
  and and_14 (and_14_out, not_4_out, not_2_out);
  and and_15 (and_15_out, in_1[1], not_4_out);
  and and_16 (and_16_out, in_1[3], in_1[2]);
  and and_17 (and_17_out, in_1[1], in_1[3]);
  and and_18 (and_18_out, in_1[1], not_4_out);
  and and_19 (and_19_out, in_1[1], not_2_out);
  and and_20 (and_20_out, not_4_out, not_2_out);
  and and_21 (and_21_out, in_1[2], not_3_out, in_1[0]);
  and and_22 (and_22_out, not_1_out, in_1[2]);
  and and_23 (and_23_out, not_2_out, not_3_out);
  and and_24 (and_24_out, not_1_out, in_1[0], not_2_out);
  and and_25 (and_25_out, in_1[2], in_1[3]);
  and and_26 (and_26_out, in_1[3], in_1[1]);
  or or_1 (A, in_1[3], and_1_out, and_2_out, and_3_out);
  or or_2 (B, in_1[3], and_4_out, and_5_out, and_6_out);
  or or_3 (C, in_1[3], and_7_out, and_8_out, and_9_out);
  or or_4 (D, and_10_out, and_11_out, and_12_out, and_13_out);
  or or_5 (E, and_14_out, and_15_out, and_16_out, and_17_out);
  or or_6 (F, in_1[3], and_18_out, and_19_out, and_20_out, and_21_out);
  or or_7 (G, and_22_out, and_23_out, and_24_out);
  or or_8 (H, and_25_out, and_26_out);
endmodule
