// Logisim project lab08.circ as structural Verilog: 3 circuits, main circuit main
module main (
  input  [3:0] ALU_Operation,
  input  [7:0] A,
  input  [7:0] B,
  output Zero,
  output [7:0] Result,
  output Overflow
);

  _8_Bit_ALU u_8_bit_alu_1 (
    .ALU_Operation(ALU_Operation), .A(A), .B(B), .Overflow(Overflow), .Zero(Zero), .Result(Result));
endmodule

module _1_Bit_ALU (
  input  [1:0] Operation,
  input  Ainverse,
  input  Binverse,
  input  Carryin,
  input  A,
  input  B,
  input  Less,
  output Result,
  output Carryout,
  output Set
);

  wire and_1_out, multiplexer_1_out, multiplexer_2_out, not_1_out, not_2_out, or_1_out;

  not not_1 (not_1_out, A);
  not not_2 (not_2_out, B);
  Multiplexer multiplexer_1 (.in0(A), .in1(not_1_out), .out(multiplexer_1_out), .sel(Ainverse));  // open: en
  Multiplexer multiplexer_2 (.in0(B), .in1(not_2_out), .out(multiplexer_2_out), .sel(Binverse));  // open: en
  and and_1 (and_1_out, multiplexer_1_out, multiplexer_2_out);
  or or_1 (or_1_out, multiplexer_1_out, multiplexer_2_out);
  Adder #(.width(1)) adder_1 (.a(multiplexer_1_out), .b(multiplexer_2_out), .out(Set), .cin(Carryin), .cout(Carryout));
  Multiplexer #(.select(2)) multiplexer_3 (
    .in0(and_1_out), .in1(or_1_out), .in2(Set), .in3(Less), .out(Result), .sel(Operation));  // open: en
endmodule

module _8_Bit_ALU (
  input  [3:0] ALU_Operation,
  input  [7:0] A,
  input  [7:0] B,
  output Zero,
  output [7:0] Result,
  output Overflow
);

  wire n1_bit_alu_1_carryout, n1_bit_alu_2_carryout, n1_bit_alu_8_set, or_1_out;

  _1_Bit_ALU u_1_bit_alu_1 (
    .A(A[0]), .B(B[0]), .Less(n1_bit_alu_8_set), .Ainverse(ALU_Operation[3]), .Binverse(ALU_Operation[2]),
    .Carryin(ALU_Operation[2]), .Operation(ALU_Operation[1:0]), .Carryout(n1_bit_alu_1_carryout),
    .Result(Result[0]));  // open: Set
  _1_Bit_ALU u_1_bit_alu_2 (
    .A(A[1]), .B(B[1]), .Less(1'b0), .Ainverse(ALU_Operation[3]), .Binverse(ALU_Operation[2]),
    .Carryin(n1_bit_alu_1_carryout), .Operation(ALU_Operation[1:0]), .Carryout(n1_bit_alu_2_carryout),
    .Result(Result[1]));  // open: Set
  _1_Bit_ALU u_1_bit_alu_3 (
    .A(A[2]), .B(B[2]), .Less(1'b0), .Ainverse(ALU_Operation[3]), .Binverse(ALU_Operation[2]),
    .Carryin(n1_bit_alu_2_carryout), .Operation(ALU_Operation[1:0]), .Result(Result[2]));  // open: Carryout, Set
  _1_Bit_ALU u_1_bit_alu_4 (
    .A(A[3]), .B(B[3]), .Less(1'b0), .Ainverse(ALU_Operation[3]), .Binverse(ALU_Operation[2]),
    .Operation(ALU_Operation[1:0]), .Result(Result[3]));  // open: Carryin, Carryout, Set
  _1_Bit_ALU u_1_bit_alu_5 (
    .A(A[4]), .B(B[4]), .Less(1'b0), .Ainverse(ALU_Operation[3]), .Binverse(ALU_Operation[2]),
    .Operation(ALU_Operation[1:0]), .Result(Result[4]));  // open: Carryin, Carryout, Set
  _1_Bit_ALU u_1_bit_alu_6 (
    .A(A[5]), .B(B[5]), .Less(1'b0), .Ainverse(ALU_Operation[3]), .Binverse(ALU_Operation[2]),
    .Operation(ALU_Operation[1:0]), .Result(Result[5]));  // open: Carryin, Carryout, Set
  _1_Bit_ALU u_1_bit_alu_7 (
    .A(A[6]), .B(B[6]), .Less(1'b0), .Ainverse(ALU_Operation[3]), .Binverse(ALU_Operation[2]),
    .Operation(ALU_Operation[1:0]), .Result(Result[6]));  // open: Carryin, Carryout, Set
  _1_Bit_ALU u_1_bit_alu_8 (
    .A(A[7]), .B(B[7]), .Ainverse(ALU_Operation[3]), .Binverse(ALU_Operation[2]),
    .Operation(ALU_Operation[1:0]), .Carryout(Overflow), .Result(Result[7]), .Set(n1_bit_alu_8_set));  // open: Less, Carryin
  or or_1 (or_1_out, Result[0], Result[1], Result[2], Result[3], Result[4], Result[5], Result[6], Result[7]);
  not not_1 (Zero, or_1_out);
endmodule
