// Logisim project project4_div_sqrt.circ as structural Verilog: 5 circuits, main circuit main
module main (
  input  [15:0] A,
  input  [15:0] B,
  input  example_instruction,
  input  division_instruction,
  input  square_root_instruction,
  output Example_Ready,
  output Division_Ready,
  output Square_Root_Ready
);

  wire clock_1_out, q8_8_to_decimal_1_decimal_point, q8_8_to_decimal_2_decimal_point,
       q8_8_to_decimal_3_decimal_point, q8_8_to_decimal_4_decimal_point, q8_8_to_decimal_5_decimal_point;
  wire [3:0] q8_8_to_decimal_1_bcd1, q8_8_to_decimal_1_bcd1_2, q8_8_to_decimal_1_bcd1_3,
       q8_8_to_decimal_1_bcd1_4, q8_8_to_decimal_1_bcd1_5, q8_8_to_decimal_1_bcd1_6, q8_8_to_decimal_1_bcd2,
       q8_8_to_decimal_2_bcd1, q8_8_to_decimal_2_bcd1_2, q8_8_to_decimal_2_bcd1_3, q8_8_to_decimal_2_bcd1_4,
       q8_8_to_decimal_2_bcd1_5, q8_8_to_decimal_2_bcd1_6, q8_8_to_decimal_2_bcd2, q8_8_to_decimal_3_bcd1,
       q8_8_to_decimal_3_bcd1_2, q8_8_to_decimal_3_bcd1_3, q8_8_to_decimal_3_bcd1_4,
       q8_8_to_decimal_3_bcd1_5, q8_8_to_decimal_3_bcd1_6, q8_8_to_decimal_3_bcd2, q8_8_to_decimal_4_bcd1,
       q8_8_to_decimal_4_bcd1_2, q8_8_to_decimal_4_bcd1_3, q8_8_to_decimal_4_bcd1_4,
       q8_8_to_decimal_4_bcd1_5, q8_8_to_decimal_4_bcd1_6, q8_8_to_decimal_4_bcd2, q8_8_to_decimal_5_bcd1,
       q8_8_to_decimal_5_bcd1_2, q8_8_to_decimal_5_bcd1_3, q8_8_to_decimal_5_bcd1_4,
       q8_8_to_decimal_5_bcd1_5, q8_8_to_decimal_5_bcd1_6, q8_8_to_decimal_5_bcd2;
  wire [15:0] division_1_quotient, example_1_result, square_root_1_result;

  Hex_Digit_Display hex_digit_display_1 (.value(q8_8_to_decimal_1_bcd2));  // open: dp
  Hex_Digit_Display hex_digit_display_2 (.value(q8_8_to_decimal_2_bcd2));  // open: dp
  Hex_Digit_Display hex_digit_display_3 (.value(q8_8_to_decimal_1_bcd1));  // open: dp
  Hex_Digit_Display hex_digit_display_4 (.value(q8_8_to_decimal_1_bcd1_2), .dp(q8_8_to_decimal_1_decimal_point));
  Q8_8_to_Decimal q8_8_to_decimal_1 (
    .Q8_8_Input(A), .BCD2(q8_8_to_decimal_1_bcd2), .BCD1(q8_8_to_decimal_1_bcd1),
    .BCD1_2(q8_8_to_decimal_1_bcd1_2), .Decimal_Point(q8_8_to_decimal_1_decimal_point),
    .BCD1_3(q8_8_to_decimal_1_bcd1_3), .BCD1_4(q8_8_to_decimal_1_bcd1_4), .BCD1_5(q8_8_to_decimal_1_bcd1_5),
    .BCD1_6(q8_8_to_decimal_1_bcd1_6));
  Hex_Digit_Display hex_digit_display_5 (.value(q8_8_to_decimal_2_bcd1_2), .dp(q8_8_to_decimal_2_decimal_point));
  Hex_Digit_Display hex_digit_display_6 (.value(q8_8_to_decimal_2_bcd1));  // open: dp
  Q8_8_to_Decimal q8_8_to_decimal_2 (
    .Q8_8_Input(B), .BCD2(q8_8_to_decimal_2_bcd2), .BCD1(q8_8_to_decimal_2_bcd1),
    .BCD1_2(q8_8_to_decimal_2_bcd1_2), .Decimal_Point(q8_8_to_decimal_2_decimal_point),
    .BCD1_3(q8_8_to_decimal_2_bcd1_3), .BCD1_4(q8_8_to_decimal_2_bcd1_4), .BCD1_5(q8_8_to_decimal_2_bcd1_5),
    .BCD1_6(q8_8_to_decimal_2_bcd1_6));
  Hex_Digit_Display hex_digit_display_7 (.value(q8_8_to_decimal_1_bcd1_3));  // open: dp
  Hex_Digit_Display hex_digit_display_8 (.value(q8_8_to_decimal_1_bcd1_4));  // open: dp
  Hex_Digit_Display hex_digit_display_9 (.value(q8_8_to_decimal_2_bcd1_4));  // open: dp
  Hex_Digit_Display hex_digit_display_10 (.value(q8_8_to_decimal_2_bcd1_3));  // open: dp
  Hex_Digit_Display hex_digit_display_11 (.value(q8_8_to_decimal_1_bcd1_6));  // open: dp
  Hex_Digit_Display hex_digit_display_12 (.value(q8_8_to_decimal_1_bcd1_5));  // open: dp
  Hex_Digit_Display hex_digit_display_13 (.value(q8_8_to_decimal_2_bcd1_5));  // open: dp
  Hex_Digit_Display hex_digit_display_14 (.value(q8_8_to_decimal_2_bcd1_6));  // open: dp
  Example example_1 (
    .A(A), .example_instruction(example_instruction), .Clock(clock_1_out), .Result(example_1_result),
    .example_ready(Example_Ready));
  Division division_1 (
    .Dividend(A), .Divisor(B), .division_instruction(division_instruction), .Clock(clock_1_out),
    .Quotient(division_1_quotient), .division_ready(Division_Ready));
  Square_Root square_root_1 (
    .Q8_8_Input(A), .square_root_instruction(square_root_instruction), .Clock(clock_1_out),
    .Result(square_root_1_result), .square_root_ready(Square_Root_Ready));
  Clock clock_1 (.out(clock_1_out));
  Hex_Digit_Display hex_digit_display_15 (.value(q8_8_to_decimal_3_bcd1));  // open: dp
  Hex_Digit_Display hex_digit_display_16 (.value(q8_8_to_decimal_3_bcd2));  // open: dp
  Hex_Digit_Display hex_digit_display_17 (.value(q8_8_to_decimal_4_bcd1));  // open: dp
  Hex_Digit_Display hex_digit_display_18 (.value(q8_8_to_decimal_4_bcd2));  // open: dp
  Hex_Digit_Display hex_digit_display_19 (.value(q8_8_to_decimal_5_bcd2));  // open: dp
  Hex_Digit_Display hex_digit_display_20 (.value(q8_8_to_decimal_5_bcd1));  // open: dp
  Hex_Digit_Display hex_digit_display_21 (.value(q8_8_to_decimal_3_bcd1_2), .dp(q8_8_to_decimal_3_decimal_point));
  Hex_Digit_Display hex_digit_display_22 (.value(q8_8_to_decimal_3_bcd1_3));  // open: dp
  Q8_8_to_Decimal q8_8_to_decimal_3 (
    .Q8_8_Input(example_1_result), .BCD2(q8_8_to_decimal_3_bcd2), .BCD1(q8_8_to_decimal_3_bcd1),
    .BCD1_2(q8_8_to_decimal_3_bcd1_2), .Decimal_Point(q8_8_to_decimal_3_decimal_point),
    .BCD1_3(q8_8_to_decimal_3_bcd1_3), .BCD1_4(q8_8_to_decimal_3_bcd1_4), .BCD1_5(q8_8_to_decimal_3_bcd1_5),
    .BCD1_6(q8_8_to_decimal_3_bcd1_6));
  Hex_Digit_Display hex_digit_display_23 (.value(q8_8_to_decimal_4_bcd1_2), .dp(q8_8_to_decimal_4_decimal_point));
  Hex_Digit_Display hex_digit_display_24 (.value(q8_8_to_decimal_4_bcd1_3));  // open: dp
  Q8_8_to_Decimal q8_8_to_decimal_4 (
    .Q8_8_Input(division_1_quotient), .BCD2(q8_8_to_decimal_4_bcd2), .BCD1(q8_8_to_decimal_4_bcd1),
    .BCD1_2(q8_8_to_decimal_4_bcd1_2), .Decimal_Point(q8_8_to_decimal_4_decimal_point),
    .BCD1_3(q8_8_to_decimal_4_bcd1_3), .BCD1_4(q8_8_to_decimal_4_bcd1_4), .BCD1_5(q8_8_to_decimal_4_bcd1_5),
    .BCD1_6(q8_8_to_decimal_4_bcd1_6));
  Hex_Digit_Display hex_digit_display_25 (.value(q8_8_to_decimal_5_bcd1_2), .dp(q8_8_to_decimal_5_decimal_point));
  Hex_Digit_Display hex_digit_display_26 (.value(q8_8_to_decimal_5_bcd1_3));  // open: dp
  Q8_8_to_Decimal q8_8_to_decimal_5 (
    .Q8_8_Input(square_root_1_result), .BCD2(q8_8_to_decimal_5_bcd2), .BCD1(q8_8_to_decimal_5_bcd1),
    .BCD1_2(q8_8_to_decimal_5_bcd1_2), .Decimal_Point(q8_8_to_decimal_5_decimal_point),
    .BCD1_3(q8_8_to_decimal_5_bcd1_3), .BCD1_4(q8_8_to_decimal_5_bcd1_4), .BCD1_5(q8_8_to_decimal_5_bcd1_5),
    .BCD1_6(q8_8_to_decimal_5_bcd1_6));
  Hex_Digit_Display hex_digit_display_27 (.value(q8_8_to_decimal_3_bcd1_5));  // open: dp
  Hex_Digit_Display hex_digit_display_28 (.value(q8_8_to_decimal_3_bcd1_4));  // open: dp
  Hex_Digit_Display hex_digit_display_29 (.value(q8_8_to_decimal_4_bcd1_4));  // open: dp
  Hex_Digit_Display hex_digit_display_30 (.value(q8_8_to_decimal_4_bcd1_5));  // open: dp
  Hex_Digit_Display hex_digit_display_31 (.value(q8_8_to_decimal_5_bcd1_5));  // open: dp
  Hex_Digit_Display hex_digit_display_32 (.value(q8_8_to_decimal_5_bcd1_4));  // open: dp
  Hex_Digit_Display hex_digit_display_33 (.value(q8_8_to_decimal_3_bcd1_6));  // open: dp
  Hex_Digit_Display hex_digit_display_34 (.value(q8_8_to_decimal_4_bcd1_6));  // open: dp
  Hex_Digit_Display hex_digit_display_35 (.value(q8_8_to_decimal_5_bcd1_6));  // open: dp
endmodule

module Q8_8_to_Decimal (
  input  [15:0] Q8_8_Input,
  output Decimal_Point,
  output [3:0] BCD2,
  output [3:0] BCD1,
  output [3:0] BCD1_2,
  output [3:0] BCD1_3,
  output [3:0] BCD1_4,
  output [3:0] BCD1_5,
  output [3:0] BCD1_6
);

  wire [15:0] divider_1_rem, divider_2_rem;
  wire [15:4] divider_1_out, divider_2_out, divider_3_out;
  wire [16:0] adder_1_out, adder_2_out, adder_3_out, adder_4_out, adder_5_out, adder_6_out, adder_7_out,
       divider_4_rem, divider_5_out, divider_6_rem, multiplexer_1_out, multiplexer_2_out, multiplexer_3_out,
       multiplexer_4_out, multiplexer_5_out, multiplexer_6_out, multiplexer_7_out, multiplexer_8_out;
  wire [16:4] divider_4_out, divider_6_out, divider_7_out, divider_7_rem;

  Divider #(.width(16)) divider_1 (
    .a(Q8_8_Input), .b(16'h6400), .out({divider_1_out, BCD2}), .rem(divider_1_rem));  // open: upper
  Divider #(.width(16)) divider_2 (
    .a(divider_1_rem), .b(16'ha00), .out({divider_2_out, BCD1}), .rem(divider_2_rem));  // open: upper
  Multiplexer #(.width(17), .enable("false")) multiplexer_1 (
    .in0({17{1'b0}}), .in1(17'hc350), .out(multiplexer_1_out), .sel(Q8_8_Input[7]));
  Multiplexer #(.width(17), .enable("false")) multiplexer_2 (
    .in0({17{1'b0}}), .in1(17'h61a8), .out(multiplexer_2_out), .sel(Q8_8_Input[6]));
  Multiplexer #(.width(17), .enable("false")) multiplexer_3 (
    .in0({17{1'b0}}), .in1(17'h30d4), .out(multiplexer_3_out), .sel(Q8_8_Input[5]));
  Multiplexer #(.width(17), .enable("false")) multiplexer_4 (
    .in0({17{1'b0}}), .in1(17'h186a), .out(multiplexer_4_out), .sel(Q8_8_Input[4]));
  Multiplexer #(.width(17), .enable("false")) multiplexer_5 (
    .in0({17{1'b0}}), .in1(17'hc35), .out(multiplexer_5_out), .sel(Q8_8_Input[3]));
  Multiplexer #(.width(17), .enable("false")) multiplexer_6 (
    .in0({17{1'b0}}), .in1(17'h61b), .out(multiplexer_6_out), .sel(Q8_8_Input[2]));
  Multiplexer #(.width(17), .enable("false")) multiplexer_7 (
    .in0({17{1'b0}}), .in1(17'h30d), .out(multiplexer_7_out), .sel(Q8_8_Input[1]));
  Multiplexer #(.width(17), .enable("false")) multiplexer_8 (
    .in0({17{1'b0}}), .in1(17'h187), .out(multiplexer_8_out), .sel(Q8_8_Input[0]));
  Divider #(.width(16)) divider_3 (.a(divider_2_rem), .b(16'h100), .out({divider_3_out, BCD1_2}));  // open: upper, rem
  Adder #(.width(17)) adder_1 (.a(multiplexer_1_out), .b(multiplexer_2_out), .out(adder_1_out));  // open: cin, cout
  Adder #(.width(17)) adder_2 (.a(multiplexer_3_out), .b(multiplexer_4_out), .out(adder_2_out));  // open: cin, cout
  Adder #(.width(17)) adder_3 (.a(multiplexer_5_out), .b(multiplexer_6_out), .out(adder_3_out));  // open: cin, cout
  Adder #(.width(17)) adder_4 (.a(multiplexer_7_out), .b(multiplexer_8_out), .out(adder_4_out));  // open: cin, cout
  Adder #(.width(17)) adder_5 (.a(adder_1_out), .b(adder_2_out), .out(adder_5_out));  // open: cin, cout
  Adder #(.width(17)) adder_6 (.a(adder_5_out), .b(adder_7_out), .out(adder_6_out));  // open: cin, cout
  Adder #(.width(17)) adder_7 (.a(adder_3_out), .b(adder_4_out), .out(adder_7_out));  // open: cin, cout
  Divider #(.width(17)) divider_4 (
    .a(divider_5_out), .b(17'h3e8), .out({divider_4_out, BCD1_3}), .rem(divider_4_rem));  // open: upper
  Divider #(.width(17)) divider_5 (.a(adder_6_out), .b(17'ha), .out(divider_5_out));  // open: upper, rem
  Divider #(.width(17)) divider_6 (
    .a(divider_4_rem), .b(17'h64), .out({divider_6_out, BCD1_4}), .rem(divider_6_rem));  // open: upper
  Divider #(.width(17)) divider_7 (
    .a(divider_6_rem), .b(17'ha), .out({divider_7_out, BCD1_5}), .rem({divider_7_rem, BCD1_6}));  // open: upper

  assign Decimal_Point = 1'b1;
endmodule

module Example (
  input  [15:0] A,
  input  example_instruction,
  input  Clock,
  output [15:0] Result,
  output example_ready
);

  wire and_1_out, not_1_out;
  wire [7:0] counter_1_q, rom_1_data;
  wire [15:0] adder_1_out, multiplexer_1_out, shifter_1_out, subtractor_1_out;

  not not_1 (not_1_out, example_instruction);
  Multiplexer #(.width(16)) multiplexer_1 (
    .in0(A), .in1(subtractor_1_out), .out(multiplexer_1_out), .sel(rom_1_data[0]));  // open: en
  Counter #(.max('h4), .ongoal("stay"), .trigger("falling")) counter_1 (
    .Q(counter_1_q), .carry(example_ready), .clk(and_1_out), .clr(not_1_out));  // open: load, D, count
  and and_1 (and_1_out, example_instruction, Clock);
  Register #(.width(16), .trigger("falling")) u_result (
    .D(multiplexer_1_out), .en(rom_1_data[1]), .Q(Result), .clk(and_1_out));  // open: clr
  ROM rom_1 (.addr(counter_1_q), .data(rom_1_data));  // open: sel
  Shifter #(.width(16)) shifter_1 (.in(Result), .\dist (4'b0001), .out(shifter_1_out));
  Adder #(.width(16)) adder_1 (.a(shifter_1_out), .b(16'h100), .out(adder_1_out));  // open: cin, cout
  Subtractor #(.width(16)) subtractor_1 (.a(adder_1_out), .b(Result), .out(subtractor_1_out));  // open: bin, bout

  // Notes on the sheet:
  //   result = A;
  //   Given an input A in Q8.8 Format,
  //   In other words, it perform the following:
  //   result = (2 * result + 1.0) - result;
  //   result = (2 * result + 1.0) - result;
  //   this circuit produces a result according to the following equation:
  //   result = (2 * ((2 * A + 1.0) - A) + 1.0) - A
  //   contents of rom_1 (hex, n*v repeats v):
  //   0 2 3 3
  //   Clock for internal registers
endmodule

module Division (
  input  [15:0] Dividend,
  input  [15:0] Divisor,
  input  division_instruction,
  input  Clock,
  output [15:0] Quotient,
  output division_ready
);

  wire and_1_out, and_2_out, comparator_1_eq, comparator_1_gt, comparator_1_lt, not_1_out, not_2_out,
       or_1_out;
  wire [7:0] counter_1_q, rom_1_data;
  wire [15:0] adder_2_out, multiplexer_6_out, shifter_4_out;
  wire [31:0] adder_1_out, bit_extender_1_out, bit_extender_2_out, Divisor_q, multiplexer_1_out,
       multiplexer_2_out, multiplexer_3_out, multiplexer_4_out, multiplexer_5_out, Remainder_q,
       shifter_1_out, shifter_2_out, shifter_3_out, subtractor_1_out;

  assign bit_extender_1_out = {{16{1'b0}}, Dividend};  // Bit_Extender bit_extender_1
  assign bit_extender_2_out = {{16{1'b0}}, Divisor};  // Bit_Extender bit_extender_2
  not not_1 (not_1_out, division_instruction);
  Shifter #(.width(32)) shifter_1 (.in(bit_extender_1_out), .\dist (5'b01000), .out(shifter_1_out));
  Multiplexer #(.width(32), .enable("false")) multiplexer_1 (
    .in0(shifter_1_out), .in1(multiplexer_4_out), .out(multiplexer_1_out), .sel(rom_1_data[0]));
  Shifter #(.width(32)) shifter_2 (.in(bit_extender_2_out), .\dist (5'b10000), .out(shifter_2_out));
  Counter #(.max('h23), .ongoal("stay"), .trigger("falling")) counter_1 (
    .Q(counter_1_q), .carry(division_ready), .clk(and_1_out), .clr(not_1_out));  // open: load, D, count
  and and_1 (and_1_out, division_instruction, Clock);
  Register #(.width(32), .trigger("falling")) Remainder (
    .D(multiplexer_1_out), .en(rom_1_data[2]), .Q(Remainder_q), .clk(and_1_out), .clr(not_2_out));
  Multiplexer #(.width(32), .enable("false")) multiplexer_2 (
    .in0(shifter_2_out), .in1(multiplexer_5_out), .out(multiplexer_2_out), .sel(rom_1_data[0]));
  ROM rom_1 (.addr(counter_1_q), .data(rom_1_data));  // open: sel
  Register #(.width(32), .trigger("falling")) u_Divisor (
    .D(multiplexer_2_out), .en(rom_1_data[1]), .Q(Divisor_q), .clk(and_1_out), .clr(not_2_out));
  not not_2 (not_2_out, division_instruction);
  Comparator #(.width(32)) comparator_1 (
    .a(Remainder_q), .b({32{1'b0}}), .gt(comparator_1_gt), .eq(comparator_1_eq), .lt(comparator_1_lt));
  Adder #(.width(32)) adder_1 (.a(Remainder_q), .b(Divisor_q), .out(adder_1_out));  // open: cin, cout
  Subtractor #(.width(32)) subtractor_1 (.a(Remainder_q), .b(Divisor_q), .out(subtractor_1_out));  // open: bin, bout
  or or_1 (or_1_out, comparator_1_gt, comparator_1_eq);
  Multiplexer #(.width(32), .enable("false")) multiplexer_3 (
    .in0(subtractor_1_out), .in1(adder_1_out), .out(multiplexer_3_out), .sel(comparator_1_lt));
  Shifter #(.width(32), .shift("lr")) shifter_3 (.in(Divisor_q), .\dist (5'b00001), .out(shifter_3_out));
  and and_2 (and_2_out, or_1_out, rom_1_data[1]);
  Multiplexer #(.width(32), .enable("false")) multiplexer_4 (
    .in0(multiplexer_3_out), .in1(Remainder_q), .out(multiplexer_4_out), .sel(and_2_out));
  Multiplexer #(.width(32), .enable("false")) multiplexer_5 (
    .in0(Divisor_q), .in1(shifter_3_out), .out(multiplexer_5_out), .sel(rom_1_data[4]));
  Multiplexer #(.width(16), .enable("false")) multiplexer_6 (
    .in0(adder_2_out), .in1(shifter_4_out), .out(multiplexer_6_out), .sel(comparator_1_lt));
  Register #(.width(16), .trigger("falling")) u_Quotient (
    .D(multiplexer_6_out), .en(rom_1_data[3]), .Q(Quotient), .clk(and_1_out), .clr(not_2_out));
  Shifter #(.width(16)) shifter_4 (.in(Quotient), .\dist (4'b0001), .out(shifter_4_out));
  Adder #(.width(16)) adder_2 (.a(shifter_4_out), .b(16'h1), .out(adder_2_out));  // open: cin, cout

  // Notes on the sheet:
  //   contents of rom_1 (hex, n*v repeats v):
  //   6 5 1f 5 1f 5 1f 5 1f 5 1f 5 1f 5 1f 5 1f 5 1f 5 1f 5 1f 5 1f 5 1f 5 1f 5 1f 5 1f 5 1f
  //   Clock for internal registers
endmodule

module Square_Root (
  input  [15:0] Q8_8_Input,
  input  square_root_instruction,
  input  Clock,
  output [15:0] Result,
  output square_root_ready
);

  wire and_1_out, comparator_1_eq, comparator_1_lt, not_1_out, or_1_out;
  wire [4:0] Counter_q, multiplexer_1_out, subtractor_1_out;
  wire [7:0] counter_2_q, rom_1_data;
  wire [15:0] adder_1_out, adder_2_out, adder_3_out, bit_extender_2_out, bit_extender_3_out,
       multiplexer_2_out, multiplier_1_out, Remainder_q, shifter_2_out, shifter_3_out, shifter_4_out,
       shifter_5_out, subtractor_2_out;
  wire [31:0] bit_extender_1_out, shifter_1_out;

  assign bit_extender_1_out = {{16{1'b0}}, Q8_8_Input};  // Bit_Extender bit_extender_1
  Multiplexer #(.width(5), .enable("false")) multiplexer_1 (
    .in0(5'b10110), .in1(subtractor_1_out), .out(multiplexer_1_out), .sel(rom_1_data[0]));
  Shifter #(.width(32), .shift("lr")) shifter_1 (.in(bit_extender_1_out), .\dist (Counter_q), .out(shifter_1_out));
  Register #(.width(5), .trigger("falling")) Counter (
    .D(multiplexer_1_out), .Q(Counter_q), .clk(and_1_out), .clr(rom_1_data[2]));  // open: en
  Counter #(.max('h13), .ongoal("stay"), .trigger("falling")) counter_2 (
    .Q(counter_2_q), .carry(square_root_ready), .clk(and_1_out), .clr(not_1_out));  // open: load, D, count
  not not_1 (not_1_out, square_root_instruction);
  and and_1 (and_1_out, square_root_instruction, Clock);
  assign bit_extender_2_out = {{14{1'b0}}, shifter_1_out[1:0]};  // Bit_Extender bit_extender_2
  Subtractor #(.width(5)) subtractor_1 (.a(Counter_q), .b(5'b00010), .out(subtractor_1_out));  // open: bin, bout
  ROM rom_1 (.addr(counter_2_q), .data(rom_1_data));  // open: sel
  Adder #(.width(16)) adder_1 (.a(bit_extender_3_out), .b(shifter_2_out), .out(adder_1_out));  // open: cin, cout
  Register #(.width(16), .trigger("falling")) u_Result (
    .D(adder_1_out), .en(rom_1_data[1]), .Q(Result), .clk(and_1_out), .clr(rom_1_data[2]));
  Shifter #(.width(16)) shifter_2 (.in(Result), .\dist (4'b0001), .out(shifter_2_out));
  Multiplexer #(.width(16), .enable("false")) multiplexer_2 (
    .in0(adder_3_out), .in1(subtractor_2_out), .out(multiplexer_2_out), .sel(or_1_out));
  Register #(.width(16), .trigger("falling")) Remainder (
    .D(multiplexer_2_out), .en(rom_1_data[0]), .Q(Remainder_q), .clk(and_1_out), .clr(rom_1_data[2]));
  Shifter #(.width(16)) shifter_3 (.in(Result), .\dist (4'b0010), .out(shifter_3_out));
  Shifter #(.width(16)) shifter_4 (.in(Remainder_q), .\dist (4'b0010), .out(shifter_4_out));
  Adder #(.width(16)) adder_2 (.a(shifter_3_out), .b(16'h1), .out(adder_2_out));  // open: cin, cout
  Adder #(.width(16)) adder_3 (.a(bit_extender_2_out), .b(shifter_4_out), .out(adder_3_out));  // open: cin, cout
  Comparator #(.width(16)) comparator_1 (
    .a(adder_2_out), .b(Remainder_q), .eq(comparator_1_eq), .lt(comparator_1_lt));  // open: gt
  or or_1 (or_1_out, comparator_1_eq, comparator_1_lt);
  assign bit_extender_3_out = {{15{1'b0}}, or_1_out};  // Bit_Extender bit_extender_3
  Subtractor #(.width(16)) subtractor_2 (
    .a(adder_3_out), .b(shifter_5_out), .out(subtractor_2_out));  // open: bin, bout
  Multiplier #(.width(16)) multiplier_1 (
    .a(adder_2_out), .b(bit_extender_3_out), .out(multiplier_1_out));  // open: cin, cout
  Shifter #(.width(16)) shifter_5 (.in(multiplier_1_out), .\dist (4'b0010), .out(shifter_5_out));

  // Notes on the sheet:
  //   contents of rom_1 (hex, n*v repeats v):
  //   4 0 17*3
  //   Clock for internal registers
endmodule
